// Logisim project HDP_Simulation_Running_Text.circ as structural Verilog: 10 circuits, main circuit Running_Text_c6ff902b
module Template (
);

  wire and_1_out, and_2_out, and_3_out, and_4_out, and_5_out, and_6_out, and_7_out, and_8_out, and_9_out,
       and_10_out, and_11_out, and_12_out, and_13_out, and_14_out, and_15_out, and_16_out, and_17_out,
       and_18_out, and_19_out, and_20_out, and_21_out, or_1_out, or_2_out, or_3_out, or_4_out, or_5_out,
       or_6_out, or_7_out, or_8_out, or_9_out, or_10_out, undriven, undriven_2, undriven_3, undriven_4,
       undriven_5, undriven_6, undriven_7, undriven_8, undriven_9, undriven_10, undriven_11, undriven_12,
       undriven_13;

  // AND_Gate and_1 has open pins: out=and_1_out
  // AND_Gate and_2 has open pins: out=and_2_out
  // AND_Gate and_3 has open pins: out=and_3_out
  // AND_Gate and_4 has open pins: out=and_4_out
  or or_1 (or_1_out, and_1_out, and_2_out);
  or or_2 (or_2_out, undriven, and_3_out);
  // AND_Gate and_5 has open pins: out=and_5_out
  // AND_Gate and_6 has open pins: out=and_6_out
  // AND_Gate and_7 has open pins: out=and_7_out
  // AND_Gate and_8 has open pins: out=and_8_out
  // AND_Gate and_9 has open pins: out=and_9_out
  // AND_Gate and_10 has open pins: out=and_10_out
  or or_3 (or_3_out, and_5_out, and_6_out, and_7_out);
  or or_4 (or_4_out, undriven_2, and_8_out, and_9_out);
  or or_5 (or_5_out, undriven_3, undriven_4, and_10_out);
  or or_6 (or_6_out, undriven_5, undriven_6, undriven_7);
  // AND_Gate and_11 has open pins: out=and_11_out
  // AND_Gate and_12 has open pins: out=and_12_out
  // AND_Gate and_13 has open pins: out=and_13_out
  // AND_Gate and_14 has open pins: out=and_14_out
  // AND_Gate and_15 has open pins: out=and_15_out
  // AND_Gate and_16 has open pins: out=and_16_out
  or or_7 (or_7_out, and_11_out, and_12_out, and_13_out, and_14_out);
  or or_8 (or_8_out, undriven_8, undriven_9, undriven_13, undriven_10);
  or or_9 (or_9_out, undriven_11, undriven_12, and_15_out, and_16_out);
  LED led_1 ();  // open: in
  LED led_2 ();  // open: in
  LED led_3 ();  // open: in
  LED led_4 ();  // open: in
  LED led_5 ();  // open: in
  LED led_6 ();  // open: in
  LED led_7 ();  // open: in
  // AND_Gate and_17 has open pins: out=and_17_out
  // AND_Gate and_18 has open pins: out=and_18_out
  // AND_Gate and_19 has open pins: out=and_19_out
  // AND_Gate and_20 has open pins: out=and_20_out
  // AND_Gate and_21 has open pins: out=and_21_out
  LED led_8 ();  // open: in
  LED led_9 ();  // open: in
  LED led_10 ();  // open: in
  LED led_11 ();  // open: in
  LED led_12 ();  // open: in
  LED led_13 ();  // open: in
  LED led_14 ();  // open: in
  LED led_15 ();  // open: in
  LED led_16 ();  // open: in
  LED led_17 ();  // open: in
  LED led_18 ();  // open: in
  LED led_19 ();  // open: in
  LED led_20 ();  // open: in
  LED led_21 ();  // open: in
  or or_10 (or_10_out, and_17_out, and_21_out);
  LED led_22 ();  // open: in
  LED led_23 ();  // open: in
  LED led_24 ();  // open: in
  LED led_25 ();  // open: in
  LED led_26 ();  // open: in
  LED led_27 ();  // open: in
  LED led_28 ();  // open: in
  LED led_29 ();  // open: in
  LED led_30 ();  // open: in
  LED led_31 ();  // open: in
  LED led_32 ();  // open: in
  LED led_33 ();  // open: in
  LED led_34 ();  // open: in
  LED led_35 ();  // open: in

  // Notes on the sheet:
  //   31,35
  //   2,4
  //   25,30
  //   31,35
  //   31,35
  //   7
  //   35
  //   26,30
  //   25
  //   25
  //   31,35
endmodule

module Clock (
  output A_,
  output B_,
  output C_,
  output D_,
  output A,
  output B,
  output C,
  output D
);

  wire clock_1_out;

  not not_1 (A, A_);
  J_K_Flip_Flop j_k_ff_1 (.J(1'b1), .K(1'b1), .clk(B_), .Q(A_));  // open: Qn, preset, reset
  J_K_Flip_Flop j_k_ff_2 (.J(1'b1), .K(1'b1), .clk(C_), .Q(B_));  // open: Qn, preset, reset
  not not_2 (B, B_);
  J_K_Flip_Flop j_k_ff_3 (.J(1'b1), .K(1'b1), .clk(D_), .Q(C_));  // open: Qn, preset, reset
  not not_3 (C, C_);
  J_K_Flip_Flop j_k_ff_4 (.J(1'b1), .K(1'b1), .clk(clock_1_out), .Q(D_));  // open: Qn, preset, reset
  Clock_part clock_1 (.out(clock_1_out));
  not not_4 (D, D_);
  // Probe on D_
  // Probe on C_
  // Probe on B_
  // Probe on A_
endmodule

module Panel_1_103ac074 (
  output _1_5_6_10,
  output _11_15,
  output _16_21_25,
  output _26_30,
  output _31_35
);

  wire and_1_out, and_2_out, and_3_out, and_4_out, and_5_out, and_6_out, and_7_out, and_8_out, and_9_out,
       and_10_out, and_11_out, and_12_out, and_13_out, and_14_out, and_15_out, and_16_out, clock_1_a,
       clock_1_a_, clock_1_b, clock_1_b_, clock_1_c, clock_1_c_, clock_1_d, clock_1_d_;

  Clock clock_1 (
    .A_(clock_1_a_), .A(clock_1_a), .B(clock_1_b), .C_(clock_1_c_), .C(clock_1_c), .D_(clock_1_d_),
    .D(clock_1_d), .B_(clock_1_b_));
  and and_1 (and_1_out, clock_1_a_, clock_1_b_);
  and and_2 (and_2_out, clock_1_b_, clock_1_c_, clock_1_d_);
  and and_3 (and_3_out, clock_1_a, clock_1_b, clock_1_c, clock_1_d);
  and and_4 (and_4_out, clock_1_a_, clock_1_b_);
  and and_5 (and_5_out, clock_1_b_, clock_1_c_, clock_1_d_);
  and and_6 (and_6_out, clock_1_b, clock_1_c, clock_1_d);
  and and_7 (and_7_out, clock_1_a_, clock_1_b_);
  and and_8 (and_8_out, clock_1_a_, clock_1_c);
  and and_9 (and_9_out, clock_1_b_, clock_1_c_, clock_1_d_);
  and and_10 (and_10_out, clock_1_b, clock_1_c, clock_1_d);
  and and_11 (and_11_out, clock_1_a_, clock_1_d);
  and and_12 (and_12_out, clock_1_a_, clock_1_c);
  and and_13 (and_13_out, clock_1_b_, clock_1_c_, clock_1_d_);
  and and_14 (and_14_out, clock_1_b, clock_1_c, clock_1_d);
  and and_15 (and_15_out, clock_1_b_, clock_1_c_, clock_1_d_);
  and and_16 (and_16_out, clock_1_b, clock_1_c, clock_1_d);
  or or_1 (_1_5_6_10, and_1_out, and_2_out, and_3_out);
  or or_2 (_11_15, and_4_out, and_5_out, and_6_out);
  or or_3 (_16_21_25, and_7_out, and_8_out, and_9_out, and_10_out);
  or or_4 (_26_30, and_11_out, and_12_out, and_13_out, and_14_out);
  or or_5 (_31_35, clock_1_a_, and_15_out, and_16_out);
  LED led_1 (.in(_1_5_6_10));
  LED led_2 ();  // open: in
  LED led_3 ();  // open: in
  LED led_4 (.in(_1_5_6_10));
  LED led_5 ();  // open: in
  LED led_6 (.in(_11_15));
  LED led_7 (.in(_16_21_25));
  LED led_8 (.in(_16_21_25));
  LED led_9 ();  // open: in
  LED led_10 (.in(_16_21_25));
  LED led_11 ();  // open: in
  LED led_12 (.in(_26_30));
  LED led_13 (.in(_31_35));
  LED led_14 ();  // open: in
  LED led_15 ();  // open: in
  LED led_16 ();  // open: in
  LED led_17 ();  // open: in
  LED led_18 ();  // open: in
  LED led_19 ();  // open: in
  LED led_20 ();  // open: in
  LED led_21 (.in(_16_21_25));
  LED led_22 (.in(_16_21_25));
  LED led_23 ();  // open: in
  LED led_24 ();  // open: in
  LED led_25 ();  // open: in
  LED led_26 ();  // open: in
  LED led_27 ();  // open: in
  LED led_28 ();  // open: in
  LED led_29 (.in(_1_5_6_10));
  LED led_30 (.in(_1_5_6_10));
  LED led_31 (.in(_11_15));
  LED led_32 (.in(_16_21_25));
  LED led_33 (.in(_16_21_25));
  LED led_34 (.in(_26_30));
  LED led_35 (.in(_31_35));
endmodule

module Panel_2_c4f6d7ff (
  output _1_5_6,
  output _2_3_4,
  output _10_15_25_30,
  output _11_16_21,
  output _26,
  output _31_35,
  output _32_33_34
);

  wire and_1_out, and_2_out, and_3_out, and_4_out, and_5_out, and_6_out, and_7_out, and_8_out, and_10_out,
       and_11_out, and_12_out, and_13_out, and_14_out, and_15_out, and_16_out, and_17_out, and_18_out,
       and_19_out, and_20_out, and_21_out, and_22_out, and_23_out, and_24_out, and_25_out, and_26_out,
       and_27_out, clock_1_a, clock_1_a_, clock_1_b, clock_1_b_, clock_1_c, clock_1_c_, clock_1_d, clock_1_d_;

  Clock clock_1 (
    .A_(clock_1_a_), .A(clock_1_a), .B(clock_1_b), .C_(clock_1_c_), .C(clock_1_c), .D_(clock_1_d_),
    .D(clock_1_d), .B_(clock_1_b_));
  and and_1 (and_1_out, clock_1_a_, clock_1_b_, clock_1_d);
  and and_2 (and_2_out, clock_1_a_, clock_1_b_, clock_1_c);
  and and_3 (and_3_out, clock_1_a, clock_1_b, clock_1_c);
  and and_4 (and_4_out, clock_1_a, clock_1_b_, clock_1_c_, clock_1_d_);
  and and_5 (and_5_out, clock_1_a_, clock_1_b_, clock_1_d);
  and and_6 (and_6_out, clock_1_a_, clock_1_b_, clock_1_c);
  and and_7 (and_7_out, clock_1_a, clock_1_b_, clock_1_c_, clock_1_d_);
  and and_8 (and_8_out, clock_1_a, clock_1_b, clock_1_c, clock_1_d);
  and and_9 (_10_15_25_30, clock_1_a, clock_1_b, clock_1_c, clock_1_d_);
  and and_10 (and_10_out, clock_1_a_, clock_1_c);
  and and_11 (and_11_out, clock_1_b, clock_1_c);
  and and_12 (and_12_out, clock_1_a_, clock_1_b_, clock_1_d);
  and and_13 (and_13_out, clock_1_a, clock_1_b_, clock_1_c_, clock_1_d_);
  and and_14 (and_14_out, clock_1_a_, clock_1_d);
  and and_15 (and_15_out, clock_1_a_, clock_1_c);
  and and_16 (and_16_out, clock_1_b, clock_1_c);
  and and_17 (and_17_out, clock_1_a, clock_1_b_, clock_1_c_, clock_1_d_);
  and and_18 (and_18_out, clock_1_a_, clock_1_d);
  and and_19 (and_19_out, clock_1_a_, clock_1_c);
  and and_20 (and_20_out, clock_1_a_, clock_1_b);
  and and_21 (and_21_out, clock_1_b, clock_1_c);
  and and_22 (and_22_out, clock_1_a, clock_1_b_, clock_1_c_, clock_1_d_);
  and and_23 (and_23_out, clock_1_a_, clock_1_d);
  and and_24 (and_24_out, clock_1_a_, clock_1_c);
  and and_25 (and_25_out, clock_1_a_, clock_1_b);
  and and_26 (and_26_out, clock_1_b, clock_1_c, clock_1_d);
  and and_27 (and_27_out, clock_1_a, clock_1_b_, clock_1_c_, clock_1_d_);
  or or_1 (_1_5_6, and_1_out, and_2_out, and_3_out, and_4_out);
  or or_2 (_2_3_4, and_5_out, and_6_out, and_7_out, and_8_out);
  or or_3 (_11_16_21, and_10_out, and_11_out, and_12_out, and_13_out);
  or or_4 (_26, and_14_out, and_15_out, and_16_out, and_17_out);
  or or_5 (_31_35, and_18_out, and_22_out);
  or or_6 (_32_33_34, and_23_out, and_27_out);
  LED led_1 (.in(_2_3_4));
  LED led_2 (.in(_1_5_6));
  LED led_3 ();  // open: in
  LED led_4 (.in(_1_5_6));
  LED led_5 (.in(_11_16_21));
  LED led_6 ();  // open: in
  LED led_7 (.in(_11_16_21));
  LED led_8 (.in(_11_16_21));
  LED led_9 (.in(_11_16_21));
  LED led_10 ();  // open: in
  LED led_11 ();  // open: in
  LED led_12 (.in(_26));
  LED led_13 (.in(_31_35));
  LED led_14 (.in(_32_33_34));
  LED led_15 (.in(_2_3_4));
  LED led_16 (.in(_2_3_4));
  LED led_17 ();  // open: in
  LED led_18 ();  // open: in
  LED led_19 ();  // open: in
  LED led_20 ();  // open: in
  LED led_21 (.in(_11_16_21));
  LED led_22 (.in(_11_16_21));
  LED led_23 ();  // open: in
  LED led_24 ();  // open: in
  LED led_25 ();  // open: in
  LED led_26 ();  // open: in
  LED led_27 (.in(_32_33_34));
  LED led_28 (.in(_32_33_34));
  LED led_29 (.in(_1_5_6));
  LED led_30 (.in(_10_15_25_30));
  LED led_31 (.in(_10_15_25_30));
  LED led_32 (.in(_11_16_21));
  LED led_33 (.in(_10_15_25_30));
  LED led_34 (.in(_10_15_25_30));
  LED led_35 (.in(_31_35));
endmodule

module Panel_3_79c1b7d0 (
  output _1_5_6,
  output _2_3_4,
  output _10,
  output _11,
  output _15,
  output _16_19_21,
  output _17_18_20,
  output _22_23,
  output _25_30,
  output _26,
  output _29,
  output _31_35,
  output _32_33_34
);

  wire and_1_out, and_2_out, and_3_out, and_4_out, and_5_out, and_6_out, and_7_out, and_8_out, and_9_out,
       and_10_out, and_11_out, and_12_out, and_13_out, and_14_out, and_15_out, and_16_out, and_17_out,
       and_18_out, and_19_out, and_20_out, and_21_out, and_22_out, and_23_out, and_24_out, and_25_out,
       and_26_out, and_27_out, and_28_out, and_30_out, and_31_out, and_32_out, and_33_out, and_34_out,
       and_35_out, and_36_out, and_37_out, and_38_out, and_39_out, and_40_out, and_41_out, and_42_out,
       clock_1_a, clock_1_a_, clock_1_b, clock_1_b_, clock_1_c, clock_1_c_, clock_1_d, clock_1_d_;

  Clock clock_1 (
    .A_(clock_1_a_), .A(clock_1_a), .B(clock_1_b), .C_(clock_1_c_), .C(clock_1_c), .D_(clock_1_d_),
    .D(clock_1_d), .B_(clock_1_b_));
  and and_1 (and_1_out, clock_1_a_, clock_1_b_, clock_1_c);
  and and_2 (and_2_out, clock_1_a, clock_1_b, clock_1_d);
  and and_3 (and_3_out, clock_1_a, clock_1_b, clock_1_c);
  and and_4 (and_4_out, clock_1_a, clock_1_b_, clock_1_c_, clock_1_d_);
  and and_5 (and_5_out, clock_1_a_, clock_1_b_, clock_1_c);
  and and_6 (and_6_out, clock_1_a, clock_1_b, clock_1_c);
  and and_7 (and_7_out, clock_1_a, clock_1_b_, clock_1_c_, clock_1_d_);
  and and_8 (and_8_out, clock_1_a_, clock_1_b_, clock_1_c);
  and and_9 (and_9_out, clock_1_a, clock_1_b, clock_1_d);
  and and_10 (and_10_out, clock_1_a, clock_1_b_, clock_1_c_, clock_1_d_);
  and and_11 (and_11_out, clock_1_a_, clock_1_b_, clock_1_c);
  and and_12 (and_12_out, clock_1_a_, clock_1_c, clock_1_d);
  and and_13 (and_13_out, clock_1_a, clock_1_b, clock_1_d);
  and and_14 (and_14_out, clock_1_a, clock_1_b, clock_1_c);
  and and_15 (and_15_out, clock_1_a, clock_1_b_, clock_1_c_, clock_1_d_);
  and and_16 (and_16_out, clock_1_a_, clock_1_b_, clock_1_c);
  and and_17 (and_17_out, clock_1_a_, clock_1_c, clock_1_d);
  and and_18 (and_18_out, clock_1_a, clock_1_b, clock_1_d);
  and and_19 (and_19_out, clock_1_a, clock_1_b_, clock_1_c_, clock_1_d_);
  and and_20 (and_20_out, clock_1_a_, clock_1_c);
  and and_21 (and_21_out, clock_1_b, clock_1_c);
  and and_22 (and_22_out, clock_1_a, clock_1_b, clock_1_d);
  and and_23 (and_23_out, clock_1_a, clock_1_b_, clock_1_c_, clock_1_d_);
  and and_24 (and_24_out, clock_1_a, clock_1_b, clock_1_c_, clock_1_d);
  and and_25 (and_25_out, clock_1_a, clock_1_b, clock_1_c, clock_1_d_);
  and and_26 (and_26_out, clock_1_a_, clock_1_c);
  and and_27 (and_27_out, clock_1_b, clock_1_c, clock_1_d);
  and and_28 (and_28_out, clock_1_a, clock_1_b_, clock_1_c_, clock_1_d_);
  and and_29 (_25_30, clock_1_a, clock_1_b, clock_1_c_, clock_1_d);
  and and_30 (and_30_out, clock_1_a_, clock_1_c);
  and and_31 (and_31_out, clock_1_b, clock_1_d);
  and and_32 (and_32_out, clock_1_b, clock_1_c);
  and and_33 (and_33_out, clock_1_a, clock_1_b_, clock_1_c_, clock_1_d_);
  and and_34 (and_34_out, clock_1_a_, clock_1_c);
  and and_35 (and_35_out, clock_1_a_, clock_1_b, clock_1_d);
  and and_36 (and_36_out, clock_1_b, clock_1_c, clock_1_d);
  and and_37 (and_37_out, clock_1_a, clock_1_b_, clock_1_c_, clock_1_d_);
  and and_38 (and_38_out, clock_1_a_, clock_1_c);
  and and_39 (and_39_out, clock_1_a_, clock_1_b);
  and and_40 (and_40_out, clock_1_b, clock_1_d);
  and and_41 (and_41_out, clock_1_b, clock_1_c);
  and and_42 (and_42_out, clock_1_a, clock_1_b_, clock_1_c_, clock_1_d_);
  and and_43 (_32_33_34, clock_1_a, clock_1_b, clock_1_c, clock_1_d_);
  or or_1 (_1_5_6, and_1_out, and_2_out, and_3_out, and_4_out);
  or or_2 (_2_3_4, and_5_out, and_6_out, and_7_out);
  or or_3 (_10, and_8_out, and_9_out, and_10_out);
  or or_4 (_11, and_11_out, and_15_out);
  or or_5 (_15, and_16_out, and_17_out, and_18_out, and_19_out);
  or or_6 (_16_19_21, and_20_out, and_21_out, and_22_out, and_23_out);
  or or_7 (_17_18_20, and_24_out, and_25_out);
  or or_8 (_22_23, and_26_out, and_27_out, and_28_out);
  or or_9 (_26, and_30_out, and_31_out, and_32_out, and_33_out);
  or or_10 (_29, and_34_out, and_35_out, and_36_out, and_37_out);
  or or_11 (_31_35, and_38_out, and_42_out);
  LED led_1 (.in(_1_5_6));
  LED led_2 (.in(_2_3_4));
  LED led_3 (.in(_1_5_6));
  LED led_4 ();  // open: in
  LED led_5 ();  // open: in
  LED led_6 (.in(_11));
  LED led_7 (.in(_17_18_20));
  LED led_8 (.in(_16_19_21));
  LED led_9 (.in(_16_19_21));
  LED led_10 (.in(_22_23));
  LED led_11 (.in(_26));
  LED led_12 ();  // open: in
  LED led_13 (.in(_31_35));
  LED led_14 (.in(_32_33_34));
  LED led_15 (.in(_2_3_4));
  LED led_16 (.in(_2_3_4));
  LED led_17 ();  // open: in
  LED led_18 ();  // open: in
  LED led_19 ();  // open: in
  LED led_20 ();  // open: in
  LED led_21 (.in(_16_19_21));
  LED led_22 (.in(_17_18_20));
  LED led_23 (.in(_22_23));
  LED led_24 ();  // open: in
  LED led_25 ();  // open: in
  LED led_26 (.in(_29));
  LED led_27 (.in(_32_33_34));
  LED led_28 (.in(_32_33_34));
  LED led_29 (.in(_1_5_6));
  LED led_30 (.in(_10));
  LED led_31 (.in(_15));
  LED led_32 (.in(_17_18_20));
  LED led_33 (.in(_25_30));
  LED led_34 (.in(_25_30));
  LED led_35 (.in(_31_35));
endmodule

module Panel_4_9819acaf (
  output _1_6,
  output _2_3_4,
  output _5,
  output _10,
  output _11,
  output _15,
  output _16_21,
  output _17_18,
  output _19_35,
  output _20,
  output _22_23_29,
  output _25,
  output _26,
  output _30,
  output _31,
  output _32_33_34
);

  wire and_1_out, and_2_out, and_3_out, and_4_out, and_5_out, and_6_out, and_7_out, and_8_out, and_9_out,
       and_10_out, and_11_out, and_12_out, and_13_out, and_14_out, and_15_out, and_16_out, and_17_out,
       and_18_out, and_19_out, and_20_out, and_21_out, and_22_out, and_24_out, and_25_out, and_26_out,
       and_27_out, and_28_out, and_29_out, and_31_out, and_32_out, and_33_out, and_34_out, and_35_out,
       and_36_out, and_37_out, and_38_out, and_39_out, and_40_out, and_41_out, and_42_out, and_43_out,
       and_44_out, and_45_out, and_46_out, and_47_out, and_48_out, and_49_out, clock_1_a, clock_1_a_,
       clock_1_b, clock_1_b_, clock_1_c, clock_1_c_, clock_1_d, clock_1_d_;

  Clock clock_1 (
    .A_(clock_1_a_), .A(clock_1_a), .B(clock_1_b), .C_(clock_1_c_), .C(clock_1_c), .D_(clock_1_d_),
    .D(clock_1_d), .B_(clock_1_b_));
  and and_1 (and_1_out, clock_1_a, clock_1_b);
  and and_2 (and_2_out, clock_1_a, clock_1_c_, clock_1_d_);
  and and_3 (and_3_out, clock_1_a_, clock_1_b_, clock_1_c, clock_1_d);
  and and_4 (and_4_out, clock_1_a, clock_1_b, clock_1_d);
  and and_5 (and_5_out, clock_1_a, clock_1_b, clock_1_c);
  and and_6 (and_6_out, clock_1_a_, clock_1_b_, clock_1_c, clock_1_d);
  and and_7 (and_7_out, clock_1_a, clock_1_b_, clock_1_c_, clock_1_d_);
  and and_8 (and_8_out, clock_1_a, clock_1_b, clock_1_c_);
  and and_9 (and_9_out, clock_1_a, clock_1_b, clock_1_d_);
  and and_10 (and_10_out, clock_1_a, clock_1_c_, clock_1_d_);
  and and_11 (and_11_out, clock_1_a, clock_1_b, clock_1_c);
  and and_12 (and_12_out, clock_1_a_, clock_1_b_, clock_1_c, clock_1_d);
  and and_13 (and_13_out, clock_1_a, clock_1_b);
  and and_14 (and_14_out, clock_1_a_, clock_1_c, clock_1_d);
  and and_15 (and_15_out, clock_1_a, clock_1_c_, clock_1_d_);
  and and_16 (and_16_out, clock_1_a, clock_1_c_, clock_1_d_);
  and and_17 (and_17_out, clock_1_a, clock_1_b, clock_1_c);
  and and_18 (and_18_out, clock_1_a_, clock_1_c, clock_1_d);
  and and_19 (and_19_out, clock_1_b, clock_1_c);
  and and_20 (and_20_out, clock_1_a, clock_1_b);
  and and_21 (and_21_out, clock_1_a_, clock_1_c, clock_1_d);
  and and_22 (and_22_out, clock_1_a, clock_1_c_, clock_1_d_);
  and and_23 (_17_18, clock_1_a, clock_1_b, clock_1_c_);
  and and_24 (and_24_out, clock_1_a, clock_1_b, clock_1_c_);
  and and_25 (and_25_out, clock_1_a, clock_1_b, clock_1_d_);
  and and_26 (and_26_out, clock_1_a, clock_1_b, clock_1_d);
  and and_27 (and_27_out, clock_1_a_, clock_1_c, clock_1_d);
  and and_28 (and_28_out, clock_1_a_, clock_1_b, clock_1_c);
  and and_29 (and_29_out, clock_1_a, clock_1_c_, clock_1_d_);
  and and_30 (_22_23_29, clock_1_a, clock_1_b, clock_1_c, clock_1_d_);
  and and_31 (and_31_out, clock_1_a_, clock_1_c, clock_1_d);
  and and_32 (and_32_out, clock_1_a_, clock_1_b, clock_1_c);
  and and_33 (and_33_out, clock_1_b, clock_1_c, clock_1_d);
  and and_34 (and_34_out, clock_1_a, clock_1_c_, clock_1_d_);
  and and_35 (and_35_out, clock_1_b, clock_1_d);
  and and_36 (and_36_out, clock_1_b, clock_1_c);
  and and_37 (and_37_out, clock_1_a_, clock_1_c, clock_1_d);
  and and_38 (and_38_out, clock_1_a, clock_1_c_, clock_1_d_);
  and and_39 (and_39_out, clock_1_a_, clock_1_c, clock_1_d);
  and and_40 (and_40_out, clock_1_a_, clock_1_b, clock_1_d);
  and and_41 (and_41_out, clock_1_a_, clock_1_b, clock_1_c);
  and and_42 (and_42_out, clock_1_b, clock_1_c, clock_1_d);
  and and_43 (and_43_out, clock_1_a, clock_1_c_, clock_1_d_);
  and and_44 (and_44_out, clock_1_a_, clock_1_c, clock_1_d);
  and and_45 (and_45_out, clock_1_a, clock_1_c_, clock_1_d_);
  and and_46 (and_46_out, clock_1_a_, clock_1_b);
  and and_47 (and_47_out, clock_1_b, clock_1_d);
  and and_48 (and_48_out, clock_1_a_, clock_1_c, clock_1_d);
  and and_49 (and_49_out, clock_1_a, clock_1_b_, clock_1_c_, clock_1_d_);
  or or_1 (_1_6, and_1_out, and_2_out, and_3_out);
  or or_2 (_2_3_4, and_4_out, and_5_out, and_6_out, and_7_out);
  or or_3 (_5, and_8_out, and_9_out);
  or or_4 (_10, and_10_out, and_11_out, and_12_out);
  or or_5 (_11, and_13_out, and_14_out, and_15_out);
  or or_6 (_15, and_16_out, and_17_out, and_18_out);
  or or_7 (_16_21, and_19_out, and_20_out, and_21_out, and_22_out);
  or or_8 (_19_35, and_24_out, and_25_out);
  or or_9 (_20, and_26_out, and_27_out, and_28_out, and_29_out);
  or or_10 (_25, and_31_out, and_32_out, and_33_out, and_34_out);
  or or_11 (_26, and_35_out, and_36_out, and_37_out, and_38_out);
  or or_12 (_30, and_39_out, and_43_out);
  or or_13 (_31, clock_1_b, and_44_out, and_45_out);
  or or_14 (_32_33_34, and_46_out, and_47_out, and_48_out, and_49_out);
  LED led_1 (.in(_1_6));
  LED led_2 (.in(_2_3_4));
  LED led_3 ();  // open: in
  LED led_4 (.in(_1_6));
  LED led_5 (.in(_11));
  LED led_6 ();  // open: in
  LED led_7 (.in(_17_18));
  LED led_8 (.in(_16_21));
  LED led_9 (.in(_22_23_29));
  LED led_10 (.in(_16_21));
  LED led_11 (.in(_26));
  LED led_12 ();  // open: in
  LED led_13 (.in(_31));
  LED led_14 (.in(_32_33_34));
  LED led_15 (.in(_2_3_4));
  LED led_16 (.in(_2_3_4));
  LED led_17 ();  // open: in
  LED led_18 ();  // open: in
  LED led_19 ();  // open: in
  LED led_20 ();  // open: in
  LED led_21 (.in(_17_18));
  LED led_22 (.in(_19_35));
  LED led_23 (.in(_22_23_29));
  LED led_24 ();  // open: in
  LED led_25 (.in(_22_23_29));
  LED led_26 ();  // open: in
  LED led_27 (.in(_32_33_34));
  LED led_28 (.in(_32_33_34));
  LED led_29 (.in(_5));
  LED led_30 (.in(_10));
  LED led_31 (.in(_15));
  LED led_32 (.in(_20));
  LED led_33 (.in(_25));
  LED led_34 (.in(_30));
  LED led_35 (.in(_19_35));
endmodule

module Panel_5_feebb4a0 (
  output out_1,
  output _2_4,
  output _3,
  output _5_19_35,
  output _8,
  output _10_15,
  output _13,
  output _17,
  output _18,
  output _20,
  output _22_29,
  output _23,
  output _25_30,
  output _28,
  output _32_34,
  output _33
);

  wire and_1_out, and_2_out, and_3_out, and_4_out, and_5_out, and_6_out, and_7_out, and_8_out, and_9_out,
       and_10_out, and_11_out, and_12_out, and_13_out, and_14_out, and_15_out, and_16_out, and_17_out,
       and_18_out, and_19_out, and_20_out, and_21_out, and_22_out, and_23_out, and_24_out, and_25_out,
       and_26_out, and_28_out, and_29_out, and_30_out, and_31_out, and_32_out, and_33_out, and_34_out,
       and_35_out, and_36_out, and_38_out, and_39_out, and_40_out, and_41_out, clock_1_a, clock_1_a_,
       clock_1_b, clock_1_b_, clock_1_c, clock_1_c_, clock_1_d, clock_1_d_;

  Clock clock_1 (
    .A_(clock_1_a_), .A(clock_1_a), .B(clock_1_b), .C_(clock_1_c_), .C(clock_1_c), .D_(clock_1_d_),
    .D(clock_1_d), .B_(clock_1_b_));
  and and_1 (and_1_out, clock_1_a, clock_1_b, clock_1_c_);
  and and_2 (and_2_out, clock_1_a, clock_1_b, clock_1_d_);
  and and_3 (and_3_out, clock_1_a, clock_1_b_, clock_1_c, clock_1_d);
  and and_4 (and_4_out, clock_1_a, clock_1_b, clock_1_c_);
  and and_5 (and_5_out, clock_1_a, clock_1_b, clock_1_d_);
  and and_6 (and_6_out, clock_1_a, clock_1_b);
  and and_7 (and_7_out, clock_1_a_, clock_1_b_, clock_1_c);
  and and_8 (and_8_out, clock_1_a, clock_1_c_, clock_1_d_);
  and and_9 (and_9_out, clock_1_a, clock_1_b, clock_1_c_);
  and and_10 (and_10_out, clock_1_a, clock_1_b_, clock_1_c, clock_1_d);
  and and_11 (and_11_out, clock_1_a_, clock_1_b_, clock_1_c);
  and and_12 (and_12_out, clock_1_a, clock_1_b_, clock_1_c_, clock_1_d_);
  and and_13 (and_13_out, clock_1_a, clock_1_b, clock_1_c, clock_1_d);
  and and_14 (and_14_out, clock_1_a, clock_1_b_, clock_1_c, clock_1_d);
  and and_15 (and_15_out, clock_1_a, clock_1_b, clock_1_c_, clock_1_d);
  and and_16 (and_16_out, clock_1_a, clock_1_b, clock_1_c, clock_1_d_);
  and and_17 (and_17_out, clock_1_a_, clock_1_b_, clock_1_c);
  and and_18 (and_18_out, clock_1_b, clock_1_c, clock_1_d);
  and and_19 (and_19_out, clock_1_a, clock_1_b_, clock_1_c_, clock_1_d_);
  and and_20 (and_20_out, clock_1_a, clock_1_b_, clock_1_c, clock_1_d);
  and and_21 (and_21_out, clock_1_a, clock_1_b, clock_1_c_, clock_1_d_);
  and and_22 (and_22_out, clock_1_a_, clock_1_c);
  and and_23 (and_23_out, clock_1_c, clock_1_d);
  and and_24 (and_24_out, clock_1_a, clock_1_c_, clock_1_d_);
  and and_25 (and_25_out, clock_1_a, clock_1_b, clock_1_d_);
  and and_26 (and_26_out, clock_1_a, clock_1_b_, clock_1_c, clock_1_d);
  and and_27 (_22_29, clock_1_a, clock_1_b, clock_1_c_, clock_1_d);
  and and_28 (and_28_out, clock_1_a_, clock_1_c);
  and and_29 (and_29_out, clock_1_a, clock_1_b, clock_1_d);
  and and_30 (and_30_out, clock_1_a, clock_1_b_, clock_1_c_, clock_1_d_);
  and and_31 (and_31_out, clock_1_a, clock_1_b_, clock_1_c, clock_1_d);
  and and_32 (and_32_out, clock_1_a, clock_1_b, clock_1_c, clock_1_d_);
  and and_33 (and_33_out, clock_1_a_, clock_1_c);
  and and_34 (and_34_out, clock_1_a_, clock_1_b, clock_1_d);
  and and_35 (and_35_out, clock_1_b, clock_1_c, clock_1_d);
  and and_36 (and_36_out, clock_1_a, clock_1_b_, clock_1_c_, clock_1_d_);
  and and_37 (_32_34, clock_1_a, clock_1_b, clock_1_d_);
  and and_38 (and_38_out, clock_1_a_, clock_1_c);
  and and_39 (and_39_out, clock_1_a_, clock_1_b);
  and and_40 (and_40_out, clock_1_b, clock_1_c);
  and and_41 (and_41_out, clock_1_a, clock_1_c_, clock_1_d_);
  or or_1 (out_1, and_1_out, and_2_out, and_3_out);
  or or_2 (_2_4, and_4_out, and_5_out);
  or or_3 (_3, and_6_out, and_7_out, and_8_out);
  or or_4 (_5_19_35, and_9_out, and_10_out);
  or or_5 (_8, and_11_out, and_12_out, and_13_out);
  or or_6 (_10_15, and_14_out, and_15_out, and_16_out);
  or or_7 (_13, and_17_out, and_18_out, and_19_out);
  or or_8 (_17, and_20_out, and_21_out);
  or or_9 (_18, and_22_out, and_23_out, and_24_out);
  or or_10 (_20, and_25_out, and_26_out);
  or or_11 (_23, and_28_out, and_29_out, and_30_out);
  or or_12 (_25_30, and_31_out, and_32_out);
  or or_13 (_28, and_33_out, and_34_out, and_35_out, and_36_out);
  or or_14 (_33, and_38_out, and_39_out, and_40_out, and_41_out);
  LED led_1 (.in(out_1));
  LED led_2 (.in(_2_4));
  LED led_3 (.in(out_1));
  LED led_4 ();  // open: in
  LED led_5 (.in(out_1));
  LED led_6 ();  // open: in
  LED led_7 (.in(_17));
  LED led_8 (.in(out_1));
  LED led_9 (.in(out_1));
  LED led_10 (.in(_22_29));
  LED led_11 (.in(out_1));
  LED led_12 ();  // open: in
  LED led_13 (.in(_32_34));
  LED led_14 (.in(out_1));
  LED led_15 (.in(_3));
  LED led_16 (.in(_2_4));
  LED led_17 ();  // open: in
  LED led_18 (.in(_8));
  LED led_19 ();  // open: in
  LED led_20 (.in(_13));
  LED led_21 (.in(_18));
  LED led_22 (.in(_5_19_35));
  LED led_23 ();  // open: in
  LED led_24 (.in(_23));
  LED led_25 (.in(_28));
  LED led_26 (.in(_22_29));
  LED led_27 (.in(_33));
  LED led_28 (.in(_32_34));
  LED led_29 (.in(_5_19_35));
  LED led_30 (.in(_10_15));
  LED led_31 (.in(_10_15));
  LED led_32 (.in(_20));
  LED led_33 (.in(_25_30));
  LED led_34 (.in(_25_30));
  LED led_35 (.in(_5_19_35));

  // Notes on the sheet:
  //   1,6,11,16,21,26,31
endmodule

module Panel_6_c65741f1 (
  output _1_6,
  output _2_4,
  output _3,
  output _5_19,
  output _7_9,
  output _8_13_28,
  output _10,
  output _11,
  output _15,
  output _16_21,
  output _17,
  output _18,
  output _20,
  output _22,
  output _23,
  output _24,
  output _25,
  output _26,
  output _29,
  output _30,
  output _31,
  output _32_34,
  output _33,
  output _35
);

  wire and_1_out, and_2_out, and_3_out, and_4_out, and_5_out, and_6_out, and_7_out, and_8_out, and_9_out,
       and_10_out, and_11_out, and_12_out, and_13_out, and_14_out, and_15_out, and_17_out, and_18_out,
       and_19_out, and_20_out, and_21_out, and_22_out, and_23_out, and_24_out, and_25_out, and_26_out,
       and_27_out, and_28_out, and_29_out, and_30_out, and_31_out, and_32_out, and_33_out, and_35_out,
       and_36_out, and_37_out, and_38_out, and_39_out, and_40_out, and_41_out, and_42_out, and_43_out,
       and_44_out, and_45_out, and_46_out, and_47_out, and_48_out, and_49_out, and_50_out, and_51_out,
       and_52_out, and_53_out, and_54_out, and_55_out, and_56_out, and_57_out, and_58_out, and_59_out,
       and_60_out, and_61_out, and_62_out, and_64_out, and_65_out, and_66_out, and_67_out, and_68_out,
       and_69_out, and_70_out, and_71_out, and_72_out, and_73_out, and_74_out, and_75_out, and_76_out,
       and_77_out, and_78_out, and_79_out, and_80_out, and_81_out, and_82_out, clock_1_a, clock_1_a_,
       clock_1_b, clock_1_b_, clock_1_c, clock_1_c_, clock_1_d, clock_1_d_;

  Clock clock_1 (
    .A_(clock_1_a_), .A(clock_1_a), .B(clock_1_b), .C_(clock_1_c_), .C(clock_1_c), .D_(clock_1_d_),
    .D(clock_1_d), .B_(clock_1_b_));
  and and_1 (and_1_out, clock_1_a, clock_1_b_, clock_1_c);
  and and_2 (and_2_out, clock_1_a, clock_1_b, clock_1_c_);
  and and_3 (and_3_out, clock_1_a, clock_1_b, clock_1_c_);
  and and_4 (and_4_out, clock_1_a, clock_1_b_, clock_1_c, clock_1_d);
  and and_5 (and_5_out, clock_1_a, clock_1_b);
  and and_6 (and_6_out, clock_1_a_, clock_1_b_, clock_1_d);
  and and_7 (and_7_out, clock_1_a_, clock_1_b_, clock_1_c);
  and and_8 (and_8_out, clock_1_b_, clock_1_c, clock_1_d);
  and and_9 (and_9_out, clock_1_a, clock_1_c_, clock_1_d_);
  and and_10 (and_10_out, clock_1_a, clock_1_b_, clock_1_c);
  and and_11 (and_11_out, clock_1_a, clock_1_b, clock_1_c_, clock_1_d_);
  and and_12 (and_12_out, clock_1_a_, clock_1_b_, clock_1_d);
  and and_13 (and_13_out, clock_1_a_, clock_1_b_, clock_1_c);
  and and_14 (and_14_out, clock_1_a, clock_1_b_, clock_1_c_, clock_1_d_);
  and and_15 (and_15_out, clock_1_a, clock_1_b, clock_1_c, clock_1_d);
  and and_16 (_8_13_28, clock_1_a, clock_1_b, clock_1_c, clock_1_d_);
  and and_17 (and_17_out, clock_1_a, clock_1_b, clock_1_c_);
  and and_18 (and_18_out, clock_1_a, clock_1_b_, clock_1_c, clock_1_d_);
  and and_19 (and_19_out, clock_1_b_, clock_1_c);
  and and_20 (and_20_out, clock_1_c, clock_1_d);
  and and_21 (and_21_out, clock_1_a_, clock_1_b_, clock_1_d);
  and and_22 (and_22_out, clock_1_a, clock_1_b_, clock_1_d_);
  and and_23 (and_23_out, clock_1_a, clock_1_b, clock_1_c_);
  and and_24 (and_24_out, clock_1_a_, clock_1_b_, clock_1_d);
  and and_25 (and_25_out, clock_1_a_, clock_1_b_, clock_1_c);
  and and_26 (and_26_out, clock_1_b, clock_1_c, clock_1_d);
  and and_27 (and_27_out, clock_1_a, clock_1_b_, clock_1_d_);
  and and_28 (and_28_out, clock_1_a, clock_1_b, clock_1_c_);
  and and_29 (and_29_out, clock_1_a_, clock_1_c);
  and and_30 (and_30_out, clock_1_c, clock_1_d);
  and and_31 (and_31_out, clock_1_a_, clock_1_b_, clock_1_d);
  and and_32 (and_32_out, clock_1_a, clock_1_b_, clock_1_d_);
  and and_33 (and_33_out, clock_1_a, clock_1_b, clock_1_c_);
  and and_34 (_17, clock_1_a, clock_1_b_, clock_1_c);
  and and_35 (and_35_out, clock_1_a, clock_1_b_, clock_1_c);
  and and_36 (and_36_out, clock_1_a, clock_1_c, clock_1_d_);
  and and_37 (and_37_out, clock_1_a_, clock_1_c);
  and and_38 (and_38_out, clock_1_b_, clock_1_c);
  and and_39 (and_39_out, clock_1_a_, clock_1_b_, clock_1_d);
  and and_40 (and_40_out, clock_1_a, clock_1_b_, clock_1_d_);
  and and_41 (and_41_out, clock_1_a, clock_1_b, clock_1_d);
  and and_42 (and_42_out, clock_1_a_, clock_1_c);
  and and_43 (and_43_out, clock_1_a_, clock_1_b_, clock_1_d);
  and and_44 (and_44_out, clock_1_b, clock_1_c, clock_1_d);
  and and_45 (and_45_out, clock_1_a, clock_1_c_, clock_1_d_);
  and and_46 (and_46_out, clock_1_a_, clock_1_c);
  and and_47 (and_47_out, clock_1_b, clock_1_c);
  and and_48 (and_48_out, clock_1_a_, clock_1_b_, clock_1_d);
  and and_49 (and_49_out, clock_1_a, clock_1_c_, clock_1_d_);
  and and_50 (and_50_out, clock_1_a_, clock_1_c);
  and and_51 (and_51_out, clock_1_a_, clock_1_b_, clock_1_d);
  and and_52 (and_52_out, clock_1_b, clock_1_c, clock_1_d);
  and and_53 (and_53_out, clock_1_a, clock_1_b_, clock_1_c_, clock_1_d_);
  and and_54 (and_54_out, clock_1_a_, clock_1_c);
  and and_55 (and_55_out, clock_1_a_, clock_1_b_, clock_1_d);
  and and_56 (and_56_out, clock_1_a, clock_1_b_, clock_1_d_);
  and and_57 (and_57_out, clock_1_a, clock_1_b, clock_1_d);
  and and_58 (and_58_out, clock_1_a_, clock_1_d);
  and and_59 (and_59_out, clock_1_a_, clock_1_c);
  and and_60 (and_60_out, clock_1_b_, clock_1_c);
  and and_61 (and_61_out, clock_1_b, clock_1_d);
  and and_62 (and_62_out, clock_1_a, clock_1_c_, clock_1_d_);
  and and_63 (_29, clock_1_a, clock_1_b, clock_1_c_, clock_1_d_);
  and and_64 (and_64_out, clock_1_a_, clock_1_d);
  and and_65 (and_65_out, clock_1_a_, clock_1_c);
  and and_66 (and_66_out, clock_1_b, clock_1_d);
  and and_67 (and_67_out, clock_1_a, clock_1_b_, clock_1_d_);
  and and_68 (and_68_out, clock_1_a_, clock_1_d);
  and and_69 (and_69_out, clock_1_a_, clock_1_c);
  and and_70 (and_70_out, clock_1_c, clock_1_d);
  and and_71 (and_71_out, clock_1_b, clock_1_c_);
  and and_72 (and_72_out, clock_1_a, clock_1_b_, clock_1_d_);
  and and_73 (and_73_out, clock_1_a, clock_1_b_, clock_1_c, clock_1_d);
  and and_74 (and_74_out, clock_1_a, clock_1_b, clock_1_c_, clock_1_d);
  and and_75 (and_75_out, clock_1_a, clock_1_b_, clock_1_c, clock_1_d);
  and and_76 (and_76_out, clock_1_a, clock_1_b, clock_1_c_, clock_1_d);
  and and_77 (and_77_out, clock_1_a, clock_1_b, clock_1_c, clock_1_d_);
  and and_78 (and_78_out, clock_1_b_, clock_1_c);
  and and_79 (and_79_out, clock_1_a_, clock_1_d);
  and and_80 (and_80_out, clock_1_a_, clock_1_b);
  and and_81 (and_81_out, clock_1_c, clock_1_d);
  and and_82 (and_82_out, clock_1_a, clock_1_c_, clock_1_d_);
  or or_1 (_1_6, and_1_out, and_2_out);
  or or_2 (_2_4, and_3_out, and_4_out);
  or or_3 (_3, and_5_out, and_9_out);
  or or_4 (_5_19, and_10_out, and_11_out);
  or or_5 (_7_9, and_12_out, and_13_out, and_14_out, and_15_out);
  or or_6 (_10, and_17_out, and_18_out);
  or or_7 (_11, and_19_out, and_23_out);
  or or_8 (_15, and_24_out, and_28_out);
  or or_9 (_16_21, and_29_out, and_33_out);
  or or_10 (_18, and_35_out, and_36_out);
  or or_11 (_20, and_37_out, and_41_out);
  or or_12 (_22, and_42_out, and_43_out, and_44_out, and_45_out);
  or or_13 (_23, and_46_out, and_47_out, and_48_out, and_49_out);
  or or_14 (_24, and_50_out, and_51_out, and_52_out, and_53_out);
  or or_15 (_25, and_54_out, and_55_out, and_56_out, and_57_out);
  or or_16 (_26, and_58_out, and_62_out);
  or or_17 (_30, and_64_out, and_65_out, and_66_out, and_67_out);
  or or_18 (_31, and_68_out, and_72_out);
  or or_19 (_32_34, and_73_out, and_74_out);
  or or_20 (_33, and_75_out, and_76_out, and_77_out);
  or or_21 (_35, and_78_out, and_82_out);
  LED led_1 (.in(_1_6));
  LED led_2 (.in(_2_4));
  LED led_3 (.in(_7_9));
  LED led_4 (.in(_1_6));
  LED led_5 (.in(_11));
  LED led_6 ();  // open: in
  LED led_7 (.in(_16_21));
  LED led_8 (.in(_17));
  LED led_9 (.in(_22));
  LED led_10 (.in(_16_21));
  LED led_11 ();  // open: in
  LED led_12 (.in(_26));
  LED led_13 (.in(_31));
  LED led_14 (.in(_32_34));
  LED led_15 (.in(_2_4));
  LED led_16 (.in(_3));
  LED led_17 (.in(_7_9));
  LED led_18 (.in(_8_13_28));
  LED led_19 ();  // open: in
  LED led_20 (.in(_8_13_28));
  LED led_21 (.in(_5_19));
  LED led_22 (.in(_18));
  LED led_23 (.in(_23));
  LED led_24 (.in(_24));
  LED led_25 (.in(_29));
  LED led_26 (.in(_8_13_28));
  LED led_27 (.in(_32_34));
  LED led_28 (.in(_33));
  LED led_29 (.in(_5_19));
  LED led_30 (.in(_10));
  LED led_31 (.in(_15));
  LED led_32 (.in(_20));
  LED led_33 (.in(_25));
  LED led_34 (.in(_30));
  LED led_35 (.in(_35));
endmodule

module Panel_7_97c94c46 (
  output _1_6,
  output _2_4,
  output _3,
  output _5,
  output _7,
  output _8_28,
  output _9_24,
  output _10,
  output _11,
  output _13,
  output _15,
  output _16_21,
  output _17,
  output _18,
  output _19,
  output _20,
  output _22,
  output _23,
  output _25,
  output _26,
  output _29,
  output _30,
  output _31,
  output _32_34,
  output _33,
  output _35
);

  wire and_1_out, and_2_out, and_3_out, and_4_out, and_5_out, and_6_out, and_7_out, and_8_out, and_9_out,
       and_10_out, and_11_out, and_14_out, and_15_out, and_16_out, and_17_out, and_18_out, and_19_out,
       and_20_out, and_21_out, and_22_out, and_23_out, and_24_out, and_25_out, and_26_out, and_27_out,
       and_28_out, and_29_out, and_30_out, and_31_out, and_32_out, and_33_out, and_34_out, and_35_out,
       and_36_out, and_37_out, and_38_out, and_39_out, and_40_out, and_41_out, and_42_out, and_43_out,
       and_44_out, and_45_out, and_46_out, and_47_out, and_48_out, and_49_out, and_51_out, and_52_out,
       and_53_out, and_54_out, and_55_out, and_56_out, and_57_out, and_58_out, and_59_out, clock_1_a,
       clock_1_a_, clock_1_b, clock_1_b_, clock_1_c, clock_1_c_, clock_1_d, clock_1_d_;

  Clock clock_1 (
    .A_(clock_1_a_), .A(clock_1_a), .B(clock_1_b), .C_(clock_1_c_), .C(clock_1_c), .D_(clock_1_d_),
    .D(clock_1_d), .B_(clock_1_b_));
  and and_1 (and_1_out, clock_1_a, clock_1_c_, clock_1_d_);
  and and_2 (and_2_out, clock_1_a, clock_1_c, clock_1_d);
  and and_3 (and_3_out, clock_1_a, clock_1_b_, clock_1_c);
  and and_4 (and_4_out, clock_1_a, clock_1_b, clock_1_c_, clock_1_d_);
  and and_5 (and_5_out, clock_1_a, clock_1_b_, clock_1_c);
  and and_6 (and_6_out, clock_1_a, clock_1_c, clock_1_d_);
  and and_7 (and_7_out, clock_1_a, clock_1_b, clock_1_c_);
  and and_8 (and_8_out, clock_1_a, clock_1_c, clock_1_d);
  and and_9 (and_9_out, clock_1_a_, clock_1_b_);
  and and_10 (and_10_out, clock_1_b_, clock_1_c_, clock_1_d_);
  and and_11 (and_11_out, clock_1_a, clock_1_b, clock_1_c);
  and and_12 (_8_28, clock_1_a, clock_1_b, clock_1_c_, clock_1_d);
  and and_13 (_9_24, clock_1_a, clock_1_b, clock_1_c, clock_1_d_);
  and and_14 (and_14_out, clock_1_a_, clock_1_b_);
  and and_15 (and_15_out, clock_1_b_, clock_1_c_);
  and and_16 (and_16_out, clock_1_a, clock_1_c_, clock_1_d_);
  and and_17 (and_17_out, clock_1_a, clock_1_c, clock_1_d);
  and and_18 (and_18_out, clock_1_c, clock_1_d);
  and and_19 (and_19_out, clock_1_a, clock_1_d_);
  and and_20 (and_20_out, clock_1_a_, clock_1_b_);
  and and_21 (and_21_out, clock_1_b_, clock_1_c_, clock_1_d_);
  and and_22 (and_22_out, clock_1_a_, clock_1_c, clock_1_d);
  and and_23 (and_23_out, clock_1_a, clock_1_b, clock_1_d);
  and and_24 (and_24_out, clock_1_a_, clock_1_b_);
  and and_25 (and_25_out, clock_1_b_, clock_1_c_);
  and and_26 (and_26_out, clock_1_c, clock_1_d);
  and and_27 (and_27_out, clock_1_a, clock_1_b, clock_1_d_);
  and and_28 (and_28_out, clock_1_a, clock_1_d_);
  and and_29 (and_29_out, clock_1_a, clock_1_b_, clock_1_c_, clock_1_d);
  and and_30 (and_30_out, clock_1_a, clock_1_b_, clock_1_c, clock_1_d_);
  and and_31 (and_31_out, clock_1_a, clock_1_c_, clock_1_d);
  and and_32 (and_32_out, clock_1_a, clock_1_b_, clock_1_c, clock_1_d_);
  and and_33 (and_33_out, clock_1_a_, clock_1_c);
  and and_34 (and_34_out, clock_1_c, clock_1_d);
  and and_35 (and_35_out, clock_1_a_, clock_1_b_);
  and and_36 (and_36_out, clock_1_b_, clock_1_c_);
  and and_37 (and_37_out, clock_1_b, clock_1_c);
  and and_38 (and_38_out, clock_1_a, clock_1_d_);
  and and_39 (and_39_out, clock_1_a, clock_1_b_, clock_1_c, clock_1_d);
  and and_40 (and_40_out, clock_1_a, clock_1_b, clock_1_c, clock_1_d_);
  and and_41 (and_41_out, clock_1_a, clock_1_b_, clock_1_c, clock_1_d);
  and and_42 (and_42_out, clock_1_a, clock_1_b, clock_1_c_, clock_1_d);
  and and_43 (and_43_out, clock_1_a, clock_1_b, clock_1_c, clock_1_d_);
  and and_44 (and_44_out, clock_1_a_, clock_1_b_);
  and and_45 (and_45_out, clock_1_b_, clock_1_c_);
  and and_46 (and_46_out, clock_1_b, clock_1_c);
  and and_47 (and_47_out, clock_1_a, clock_1_c_, clock_1_d_);
  and and_48 (and_48_out, clock_1_a_, clock_1_d);
  and and_49 (and_49_out, clock_1_a, clock_1_d_);
  and and_50 (_29, clock_1_a, clock_1_b_, clock_1_c, clock_1_d);
  and and_51 (and_51_out, clock_1_a_, clock_1_b_);
  and and_52 (and_52_out, clock_1_b_, clock_1_c_);
  and and_53 (and_53_out, clock_1_a_, clock_1_d);
  and and_54 (and_54_out, clock_1_b, clock_1_c);
  and and_55 (and_55_out, clock_1_a, clock_1_c_, clock_1_d_);
  and and_56 (and_56_out, clock_1_a, clock_1_b_, clock_1_c, clock_1_d_);
  and and_57 (and_57_out, clock_1_a, clock_1_b, clock_1_c_, clock_1_d_);
  and and_58 (and_58_out, clock_1_a, clock_1_b, clock_1_c_);
  and and_59 (and_59_out, clock_1_a, clock_1_b_, clock_1_c, clock_1_d_);
  or or_1 (_1_6, clock_1_b_, and_1_out, and_2_out);
  or or_2 (_2_4, and_3_out, and_4_out);
  or or_3 (_3, and_5_out, and_6_out, and_7_out);
  or or_4 (_5, clock_1_b_, and_8_out);
  or or_5 (_7, and_9_out, and_10_out, and_11_out);
  or or_6 (_10, and_14_out, and_15_out, and_16_out, and_17_out);
  or or_7 (_11, clock_1_b_, and_18_out, and_19_out);
  or or_8 (_13, and_20_out, and_21_out, and_22_out, and_23_out);
  or or_9 (_15, and_24_out, and_25_out, and_26_out, and_27_out);
  or or_10 (_16_21, clock_1_b_, clock_1_c, and_28_out);
  or or_11 (_17, and_29_out, and_30_out);
  or or_12 (_18, and_31_out, and_32_out);
  or or_13 (_19, clock_1_b_, and_33_out, and_34_out);
  or or_14 (_20, and_35_out, and_36_out, and_37_out, and_38_out);
  or or_15 (_22, and_39_out, and_40_out);
  or or_16 (_23, and_41_out, and_42_out, and_43_out);
  or or_17 (_25, and_44_out, and_45_out, and_46_out, and_47_out);
  or or_18 (_26, clock_1_b_, clock_1_c, and_48_out, and_49_out);
  or or_19 (_30, and_51_out, and_55_out);
  or or_20 (_31, clock_1_a_, clock_1_b_, clock_1_d_, clock_1_c);
  or or_21 (_32_34, and_56_out, and_57_out);
  or or_22 (_33, and_58_out, and_59_out);
  or or_23 (_35, clock_1_a_, clock_1_b_, clock_1_c);
  LED led_1 (.in(_1_6));
  LED led_2 (.in(_2_4));
  LED led_3 (.in(_7));
  LED led_4 (.in(_1_6));
  LED led_5 ();  // open: in
  LED led_6 (.in(_11));
  LED led_7 (.in(_16_21));
  LED led_8 (.in(_17));
  LED led_9 (.in(_16_21));
  LED led_10 (.in(_22));
  LED led_11 (.in(_26));
  LED led_12 ();  // open: in
  LED led_13 (.in(_31));
  LED led_14 (.in(_32_34));
  LED led_15 (.in(_2_4));
  LED led_16 (.in(_3));
  LED led_17 (.in(_8_28));
  LED led_18 (.in(_9_24));
  LED led_19 ();  // open: in
  LED led_20 (.in(_13));
  LED led_21 (.in(_18));
  LED led_22 (.in(_19));
  LED led_23 (.in(_23));
  LED led_24 (.in(_9_24));
  LED led_25 (.in(_29));
  LED led_26 (.in(_8_28));
  LED led_27 (.in(_33));
  LED led_28 (.in(_32_34));
  LED led_29 (.in(_5));
  LED led_30 (.in(_10));
  LED led_31 (.in(_15));
  LED led_32 (.in(_20));
  LED led_33 (.in(_25));
  LED led_34 (.in(_30));
  LED led_35 (.in(_35));
endmodule

module Running_Text_c6ff902b (
);

  wire panel_1_103ac074_1__1_5_6_10, panel_1_103ac074_1__11_15, panel_1_103ac074_1__16_21_25,
       panel_1_103ac074_1__26_30, panel_1_103ac074_1__31_35, panel_2_c4f6d7ff_1__1_5_6,
       panel_2_c4f6d7ff_1__2_3_4, panel_2_c4f6d7ff_1__10_15_25_30, panel_2_c4f6d7ff_1__11_16_21,
       panel_2_c4f6d7ff_1__26, panel_2_c4f6d7ff_1__31_35, panel_2_c4f6d7ff_1__32_33_34,
       panel_3_79c1b7d0_1__1_5_6, panel_3_79c1b7d0_1__2_3_4, panel_3_79c1b7d0_1__10, panel_3_79c1b7d0_1__11,
       panel_3_79c1b7d0_1__15, panel_3_79c1b7d0_1__16_19_21, panel_3_79c1b7d0_1__17_18_20,
       panel_3_79c1b7d0_1__22_23, panel_3_79c1b7d0_1__25_30, panel_3_79c1b7d0_1__26, panel_3_79c1b7d0_1__29,
       panel_3_79c1b7d0_1__31_35, panel_3_79c1b7d0_1__32_33_34, panel_4_9819acaf_1__1_6,
       panel_4_9819acaf_1__2_3_4, panel_4_9819acaf_1__5, panel_4_9819acaf_1__10, panel_4_9819acaf_1__11,
       panel_4_9819acaf_1__15, panel_4_9819acaf_1__16_21, panel_4_9819acaf_1__17_18,
       panel_4_9819acaf_1__19_35, panel_4_9819acaf_1__20, panel_4_9819acaf_1__22_23_29,
       panel_4_9819acaf_1__25, panel_4_9819acaf_1__26, panel_4_9819acaf_1__30, panel_4_9819acaf_1__31,
       panel_4_9819acaf_1__32_33_34, panel_5_feebb4a0_1__2_4, panel_5_feebb4a0_1__3,
       panel_5_feebb4a0_1__5_19_35, panel_5_feebb4a0_1__8, panel_5_feebb4a0_1__10_15, panel_5_feebb4a0_1__13,
       panel_5_feebb4a0_1__17, panel_5_feebb4a0_1__18, panel_5_feebb4a0_1__20, panel_5_feebb4a0_1__22_29,
       panel_5_feebb4a0_1__23, panel_5_feebb4a0_1__25_30, panel_5_feebb4a0_1__28, panel_5_feebb4a0_1__32_34,
       panel_5_feebb4a0_1__33, panel_5_feebb4a0_1_out_1, panel_6_c65741f1_1__1_6, panel_6_c65741f1_1__2_4,
       panel_6_c65741f1_1__3, panel_6_c65741f1_1__5_19, panel_6_c65741f1_1__7_9, panel_6_c65741f1_1__8_13_28,
       panel_6_c65741f1_1__10, panel_6_c65741f1_1__11, panel_6_c65741f1_1__15, panel_6_c65741f1_1__16_21,
       panel_6_c65741f1_1__17, panel_6_c65741f1_1__18, panel_6_c65741f1_1__20, panel_6_c65741f1_1__22,
       panel_6_c65741f1_1__23, panel_6_c65741f1_1__24, panel_6_c65741f1_1__25, panel_6_c65741f1_1__26,
       panel_6_c65741f1_1__29, panel_6_c65741f1_1__30, panel_6_c65741f1_1__31, panel_6_c65741f1_1__32_34,
       panel_6_c65741f1_1__33, panel_6_c65741f1_1__35, panel_7_97c94c46_1__1_6, panel_7_97c94c46_1__2_4,
       panel_7_97c94c46_1__3, panel_7_97c94c46_1__5, panel_7_97c94c46_1__7, panel_7_97c94c46_1__8_28,
       panel_7_97c94c46_1__9_24, panel_7_97c94c46_1__10, panel_7_97c94c46_1__11, panel_7_97c94c46_1__13,
       panel_7_97c94c46_1__15, panel_7_97c94c46_1__16_21, panel_7_97c94c46_1__17, panel_7_97c94c46_1__18,
       panel_7_97c94c46_1__19, panel_7_97c94c46_1__20, panel_7_97c94c46_1__22, panel_7_97c94c46_1__23,
       panel_7_97c94c46_1__25, panel_7_97c94c46_1__26, panel_7_97c94c46_1__29, panel_7_97c94c46_1__30,
       panel_7_97c94c46_1__31, panel_7_97c94c46_1__32_34, panel_7_97c94c46_1__33, panel_7_97c94c46_1__35;

  LED led_1 (.in(panel_1_103ac074_1__1_5_6_10));
  LED led_2 (.in(panel_1_103ac074_1__1_5_6_10));
  LED led_3 (.in(panel_1_103ac074_1__11_15));
  LED led_4 (.in(panel_1_103ac074_1__16_21_25));
  LED led_5 (.in(panel_1_103ac074_1__16_21_25));
  LED led_6 (.in(panel_1_103ac074_1__26_30));
  LED led_7 (.in(panel_1_103ac074_1__31_35));
  LED led_8 ();  // open: in
  LED led_9 ();  // open: in
  LED led_10 ();  // open: in
  LED led_11 ();  // open: in
  LED led_12 ();  // open: in
  LED led_13 ();  // open: in
  LED led_14 (.in(panel_1_103ac074_1__16_21_25));
  LED led_15 (.in(panel_1_103ac074_1__16_21_25));
  LED led_16 ();  // open: in
  LED led_17 ();  // open: in
  LED led_18 ();  // open: in
  LED led_19 ();  // open: in
  LED led_20 ();  // open: in
  LED led_21 ();  // open: in
  LED led_22 ();  // open: in
  LED led_23 (.in(panel_1_103ac074_1__1_5_6_10));
  LED led_24 (.in(panel_1_103ac074_1__1_5_6_10));
  LED led_25 ();  // open: in
  LED led_26 (.in(panel_1_103ac074_1__11_15));
  LED led_27 ();  // open: in
  LED led_28 (.in(panel_1_103ac074_1__16_21_25));
  LED led_29 (.in(panel_1_103ac074_1__16_21_25));
  LED led_30 ();  // open: in
  LED led_31 (.in(panel_1_103ac074_1__16_21_25));
  LED led_32 ();  // open: in
  LED led_33 (.in(panel_1_103ac074_1__26_30));
  LED led_34 (.in(panel_1_103ac074_1__31_35));
  LED led_35 ();  // open: in
  Panel_1_103ac074 panel_1_103ac074_1 (
    ._1_5_6_10(panel_1_103ac074_1__1_5_6_10), ._11_15(panel_1_103ac074_1__11_15),
    ._16_21_25(panel_1_103ac074_1__16_21_25), ._26_30(panel_1_103ac074_1__26_30),
    ._31_35(panel_1_103ac074_1__31_35));
  LED led_36 (.in(panel_2_c4f6d7ff_1__2_3_4));
  LED led_37 (.in(panel_2_c4f6d7ff_1__1_5_6));
  LED led_38 (.in(panel_2_c4f6d7ff_1__1_5_6));
  LED led_39 ();  // open: in
  LED led_40 (.in(panel_2_c4f6d7ff_1__11_16_21));
  LED led_41 ();  // open: in
  LED led_42 (.in(panel_2_c4f6d7ff_1__11_16_21));
  LED led_43 (.in(panel_2_c4f6d7ff_1__11_16_21));
  LED led_44 ();  // open: in
  LED led_45 (.in(panel_2_c4f6d7ff_1__11_16_21));
  LED led_46 (.in(panel_2_c4f6d7ff_1__26));
  LED led_47 ();  // open: in
  LED led_48 (.in(panel_2_c4f6d7ff_1__32_33_34));
  LED led_49 (.in(panel_2_c4f6d7ff_1__31_35));
  LED led_50 (.in(panel_2_c4f6d7ff_1__2_3_4));
  LED led_51 (.in(panel_2_c4f6d7ff_1__2_3_4));
  LED led_52 ();  // open: in
  LED led_53 ();  // open: in
  LED led_54 ();  // open: in
  LED led_55 ();  // open: in
  LED led_56 (.in(panel_2_c4f6d7ff_1__11_16_21));
  LED led_57 (.in(panel_2_c4f6d7ff_1__11_16_21));
  LED led_58 ();  // open: in
  LED led_59 ();  // open: in
  LED led_60 ();  // open: in
  LED led_61 ();  // open: in
  LED led_62 (.in(panel_2_c4f6d7ff_1__32_33_34));
  LED led_63 (.in(panel_2_c4f6d7ff_1__32_33_34));
  LED led_64 (.in(panel_2_c4f6d7ff_1__1_5_6));
  LED led_65 (.in(panel_2_c4f6d7ff_1__10_15_25_30));
  LED led_66 (.in(panel_2_c4f6d7ff_1__10_15_25_30));
  LED led_67 (.in(panel_2_c4f6d7ff_1__11_16_21));
  LED led_68 (.in(panel_2_c4f6d7ff_1__10_15_25_30));
  LED led_69 (.in(panel_2_c4f6d7ff_1__10_15_25_30));
  LED led_70 (.in(panel_2_c4f6d7ff_1__31_35));
  Panel_2_c4f6d7ff panel_2_c4f6d7ff_1 (
    ._1_5_6(panel_2_c4f6d7ff_1__1_5_6), ._2_3_4(panel_2_c4f6d7ff_1__2_3_4),
    ._10_15_25_30(panel_2_c4f6d7ff_1__10_15_25_30), ._11_16_21(panel_2_c4f6d7ff_1__11_16_21),
    ._26(panel_2_c4f6d7ff_1__26), ._31_35(panel_2_c4f6d7ff_1__31_35), ._32_33_34(panel_2_c4f6d7ff_1__32_33_34));
  LED led_71 (.in(panel_3_79c1b7d0_1__1_5_6));
  LED led_72 (.in(panel_3_79c1b7d0_1__2_3_4));
  LED led_73 (.in(panel_3_79c1b7d0_1__1_5_6));
  LED led_74 ();  // open: in
  LED led_75 ();  // open: in
  LED led_76 (.in(panel_3_79c1b7d0_1__11));
  LED led_77 (.in(panel_3_79c1b7d0_1__16_19_21));
  LED led_78 (.in(panel_3_79c1b7d0_1__17_18_20));
  LED led_79 (.in(panel_3_79c1b7d0_1__22_23));
  LED led_80 (.in(panel_3_79c1b7d0_1__16_19_21));
  LED led_81 ();  // open: in
  LED led_82 (.in(panel_3_79c1b7d0_1__26));
  LED led_83 (.in(panel_3_79c1b7d0_1__32_33_34));
  LED led_84 (.in(panel_3_79c1b7d0_1__31_35));
  LED led_85 (.in(panel_3_79c1b7d0_1__2_3_4));
  LED led_86 (.in(panel_3_79c1b7d0_1__2_3_4));
  LED led_87 ();  // open: in
  LED led_88 ();  // open: in
  LED led_89 ();  // open: in
  LED led_90 ();  // open: in
  LED led_91 (.in(panel_3_79c1b7d0_1__17_18_20));
  LED led_92 (.in(panel_3_79c1b7d0_1__16_19_21));
  LED led_93 ();  // open: in
  LED led_94 (.in(panel_3_79c1b7d0_1__22_23));
  LED led_95 (.in(panel_3_79c1b7d0_1__29));
  LED led_96 ();  // open: in
  LED led_97 (.in(panel_3_79c1b7d0_1__32_33_34));
  LED led_98 (.in(panel_3_79c1b7d0_1__32_33_34));
  LED led_99 (.in(panel_3_79c1b7d0_1__1_5_6));
  LED led_100 (.in(panel_3_79c1b7d0_1__10));
  LED led_101 (.in(panel_3_79c1b7d0_1__15));
  LED led_102 (.in(panel_3_79c1b7d0_1__17_18_20));
  LED led_103 (.in(panel_3_79c1b7d0_1__25_30));
  LED led_104 (.in(panel_3_79c1b7d0_1__25_30));
  LED led_105 (.in(panel_3_79c1b7d0_1__31_35));
  Panel_3_79c1b7d0 panel_3_79c1b7d0_1 (
    ._1_5_6(panel_3_79c1b7d0_1__1_5_6), ._2_3_4(panel_3_79c1b7d0_1__2_3_4), ._10(panel_3_79c1b7d0_1__10),
    ._11(panel_3_79c1b7d0_1__11), ._15(panel_3_79c1b7d0_1__15), ._16_19_21(panel_3_79c1b7d0_1__16_19_21),
    ._17_18_20(panel_3_79c1b7d0_1__17_18_20), ._22_23(panel_3_79c1b7d0_1__22_23),
    ._25_30(panel_3_79c1b7d0_1__25_30), ._26(panel_3_79c1b7d0_1__26), ._29(panel_3_79c1b7d0_1__29),
    ._31_35(panel_3_79c1b7d0_1__31_35), ._32_33_34(panel_3_79c1b7d0_1__32_33_34));
  LED led_106 (.in(panel_4_9819acaf_1__1_6));
  LED led_107 (.in(panel_4_9819acaf_1__1_6));
  LED led_108 (.in(panel_4_9819acaf_1__11));
  LED led_109 (.in(panel_4_9819acaf_1__16_21));
  LED led_110 (.in(panel_4_9819acaf_1__16_21));
  LED led_111 (.in(panel_4_9819acaf_1__26));
  LED led_112 (.in(panel_4_9819acaf_1__31));
  LED led_113 (.in(panel_4_9819acaf_1__2_3_4));
  LED led_114 (.in(panel_4_9819acaf_1__2_3_4));
  LED led_115 ();  // open: in
  LED led_116 ();  // open: in
  LED led_117 ();  // open: in
  LED led_118 ();  // open: in
  LED led_119 (.in(panel_4_9819acaf_1__17_18));
  LED led_120 (.in(panel_4_9819acaf_1__17_18));
  LED led_121 (.in(panel_4_9819acaf_1__22_23_29));
  LED led_122 (.in(panel_4_9819acaf_1__22_23_29));
  LED led_123 ();  // open: in
  LED led_124 ();  // open: in
  LED led_125 (.in(panel_4_9819acaf_1__32_33_34));
  LED led_126 (.in(panel_4_9819acaf_1__32_33_34));
  LED led_127 (.in(panel_4_9819acaf_1__5));
  LED led_128 (.in(panel_4_9819acaf_1__2_3_4));
  LED led_129 (.in(panel_4_9819acaf_1__10));
  LED led_130 ();  // open: in
  LED led_131 (.in(panel_4_9819acaf_1__15));
  LED led_132 ();  // open: in
  LED led_133 (.in(panel_4_9819acaf_1__19_35));
  LED led_134 (.in(panel_4_9819acaf_1__20));
  LED led_135 ();  // open: in
  LED led_136 (.in(panel_4_9819acaf_1__25));
  LED led_137 (.in(panel_4_9819acaf_1__30));
  LED led_138 (.in(panel_4_9819acaf_1__22_23_29));
  LED led_139 (.in(panel_4_9819acaf_1__32_33_34));
  LED led_140 (.in(panel_4_9819acaf_1__19_35));
  LED led_141 (.in(panel_5_feebb4a0_1_out_1));
  LED led_142 (.in(panel_5_feebb4a0_1_out_1));
  LED led_143 (.in(panel_5_feebb4a0_1_out_1));
  LED led_144 (.in(panel_5_feebb4a0_1_out_1));
  LED led_145 (.in(panel_5_feebb4a0_1_out_1));
  LED led_146 (.in(panel_5_feebb4a0_1_out_1));
  LED led_147 (.in(panel_5_feebb4a0_1_out_1));
  Panel_4_9819acaf panel_4_9819acaf_1 (
    ._1_6(panel_4_9819acaf_1__1_6), ._2_3_4(panel_4_9819acaf_1__2_3_4), ._5(panel_4_9819acaf_1__5),
    ._10(panel_4_9819acaf_1__10), ._11(panel_4_9819acaf_1__11), ._15(panel_4_9819acaf_1__15),
    ._16_21(panel_4_9819acaf_1__16_21), ._17_18(panel_4_9819acaf_1__17_18),
    ._19_35(panel_4_9819acaf_1__19_35), ._20(panel_4_9819acaf_1__20),
    ._22_23_29(panel_4_9819acaf_1__22_23_29), ._25(panel_4_9819acaf_1__25), ._26(panel_4_9819acaf_1__26),
    ._30(panel_4_9819acaf_1__30), ._31(panel_4_9819acaf_1__31), ._32_33_34(panel_4_9819acaf_1__32_33_34));
  LED led_148 (.in(panel_5_feebb4a0_1__3));
  LED led_149 (.in(panel_5_feebb4a0_1__2_4));
  LED led_150 (.in(panel_5_feebb4a0_1__8));
  LED led_151 ();  // open: in
  LED led_152 (.in(panel_5_feebb4a0_1__13));
  LED led_153 ();  // open: in
  LED led_154 (.in(panel_5_feebb4a0_1__17));
  LED led_155 (.in(panel_5_feebb4a0_1__18));
  LED led_156 (.in(panel_5_feebb4a0_1__22_29));
  LED led_157 (.in(panel_5_feebb4a0_1__23));
  LED led_158 ();  // open: in
  LED led_159 (.in(panel_5_feebb4a0_1__28));
  LED led_160 (.in(panel_5_feebb4a0_1__33));
  LED led_161 (.in(panel_5_feebb4a0_1__32_34));
  LED led_162 (.in(panel_5_feebb4a0_1__2_4));
  LED led_163 (.in(panel_5_feebb4a0_1__5_19_35));
  LED led_164 ();  // open: in
  LED led_165 (.in(panel_5_feebb4a0_1__10_15));
  LED led_166 (.in(panel_5_feebb4a0_1__10_15));
  LED led_167 ();  // open: in
  LED led_168 (.in(panel_5_feebb4a0_1__20));
  LED led_169 (.in(panel_5_feebb4a0_1__5_19_35));
  LED led_170 (.in(panel_5_feebb4a0_1__25_30));
  LED led_171 ();  // open: in
  LED led_172 (.in(panel_5_feebb4a0_1__25_30));
  LED led_173 (.in(panel_5_feebb4a0_1__23));
  LED led_174 (.in(panel_5_feebb4a0_1__32_34));
  LED led_175 (.in(panel_5_feebb4a0_1__5_19_35));
  Panel_5_feebb4a0 panel_5_feebb4a0_1 (
    .out_1(panel_5_feebb4a0_1_out_1), ._2_4(panel_5_feebb4a0_1__2_4), ._3(panel_5_feebb4a0_1__3),
    ._5_19_35(panel_5_feebb4a0_1__5_19_35), ._8(panel_5_feebb4a0_1__8), ._10_15(panel_5_feebb4a0_1__10_15),
    ._13(panel_5_feebb4a0_1__13), ._17(panel_5_feebb4a0_1__17), ._18(panel_5_feebb4a0_1__18),
    ._20(panel_5_feebb4a0_1__20), ._22_29(panel_5_feebb4a0_1__22_29), ._23(panel_5_feebb4a0_1__23),
    ._25_30(panel_5_feebb4a0_1__25_30), ._28(panel_5_feebb4a0_1__28), ._32_34(panel_5_feebb4a0_1__32_34),
    ._33(panel_5_feebb4a0_1__33));
  LED led_176 (.in(panel_6_c65741f1_1__1_6));
  LED led_177 (.in(panel_6_c65741f1_1__2_4));
  LED led_178 (.in(panel_6_c65741f1_1__7_9));
  LED led_179 (.in(panel_6_c65741f1_1__1_6));
  LED led_180 ();  // open: in
  LED led_181 (.in(panel_6_c65741f1_1__11));
  LED led_182 (.in(panel_6_c65741f1_1__17));
  LED led_183 (.in(panel_6_c65741f1_1__16_21));
  LED led_184 (.in(panel_6_c65741f1_1__22));
  LED led_185 (.in(panel_6_c65741f1_1__16_21));
  LED led_186 (.in(panel_6_c65741f1_1__26));
  LED led_187 ();  // open: in
  LED led_188 (.in(panel_6_c65741f1_1__31));
  LED led_189 (.in(panel_6_c65741f1_1__32_34));
  LED led_190 (.in(panel_6_c65741f1_1__2_4));
  LED led_191 (.in(panel_6_c65741f1_1__3));
  LED led_192 (.in(panel_6_c65741f1_1__8_13_28));
  LED led_193 (.in(panel_6_c65741f1_1__7_9));
  LED led_194 (.in(panel_6_c65741f1_1__8_13_28));
  LED led_195 ();  // open: in
  LED led_196 (.in(panel_6_c65741f1_1__18));
  LED led_197 (.in(panel_6_c65741f1_1__5_19));
  LED led_198 (.in(panel_6_c65741f1_1__24));
  LED led_199 (.in(panel_6_c65741f1_1__23));
  LED led_200 (.in(panel_6_c65741f1_1__8_13_28));
  LED led_201 (.in(panel_6_c65741f1_1__29));
  LED led_202 (.in(panel_6_c65741f1_1__33));
  LED led_203 (.in(panel_6_c65741f1_1__32_34));
  LED led_204 (.in(panel_6_c65741f1_1__5_19));
  LED led_205 (.in(panel_6_c65741f1_1__10));
  LED led_206 (.in(panel_6_c65741f1_1__15));
  LED led_207 (.in(panel_6_c65741f1_1__20));
  LED led_208 (.in(panel_6_c65741f1_1__25));
  LED led_209 (.in(panel_6_c65741f1_1__30));
  LED led_210 (.in(panel_6_c65741f1_1__35));
  Panel_6_c65741f1 panel_6_c65741f1_1 (
    ._1_6(panel_6_c65741f1_1__1_6), ._2_4(panel_6_c65741f1_1__2_4), ._3(panel_6_c65741f1_1__3),
    ._5_19(panel_6_c65741f1_1__5_19), ._7_9(panel_6_c65741f1_1__7_9), ._8_13_28(panel_6_c65741f1_1__8_13_28),
    ._10(panel_6_c65741f1_1__10), ._11(panel_6_c65741f1_1__11), ._15(panel_6_c65741f1_1__15),
    ._16_21(panel_6_c65741f1_1__16_21), ._17(panel_6_c65741f1_1__17), ._18(panel_6_c65741f1_1__18),
    ._20(panel_6_c65741f1_1__20), ._22(panel_6_c65741f1_1__22), ._23(panel_6_c65741f1_1__23),
    ._24(panel_6_c65741f1_1__24), ._25(panel_6_c65741f1_1__25), ._26(panel_6_c65741f1_1__26),
    ._29(panel_6_c65741f1_1__29), ._30(panel_6_c65741f1_1__30), ._31(panel_6_c65741f1_1__31),
    ._32_34(panel_6_c65741f1_1__32_34), ._33(panel_6_c65741f1_1__33), ._35(panel_6_c65741f1_1__35));
  LED led_211 (.in(panel_7_97c94c46_1__2_4));
  LED led_212 (.in(panel_7_97c94c46_1__1_6));
  LED led_213 (.in(panel_7_97c94c46_1__1_6));
  LED led_214 (.in(panel_7_97c94c46_1__7));
  LED led_215 ();  // open: in
  LED led_216 (.in(panel_7_97c94c46_1__11));
  LED led_217 (.in(panel_7_97c94c46_1__17));
  LED led_218 (.in(panel_7_97c94c46_1__16_21));
  LED led_219 (.in(panel_7_97c94c46_1__16_21));
  LED led_220 (.in(panel_7_97c94c46_1__22));
  LED led_221 ();  // open: in
  LED led_222 (.in(panel_7_97c94c46_1__26));
  LED led_223 (.in(panel_7_97c94c46_1__32_34));
  LED led_224 (.in(panel_7_97c94c46_1__31));
  LED led_225 (.in(panel_7_97c94c46_1__3));
  LED led_226 (.in(panel_7_97c94c46_1__2_4));
  LED led_227 (.in(panel_7_97c94c46_1__8_28));
  LED led_228 (.in(panel_7_97c94c46_1__9_24));
  LED led_229 ();  // open: in
  LED led_230 (.in(panel_7_97c94c46_1__13));
  LED led_231 (.in(panel_7_97c94c46_1__19));
  LED led_232 (.in(panel_7_97c94c46_1__18));
  LED led_233 (.in(panel_7_97c94c46_1__23));
  LED led_234 (.in(panel_7_97c94c46_1__9_24));
  LED led_235 (.in(panel_7_97c94c46_1__29));
  LED led_236 (.in(panel_7_97c94c46_1__8_28));
  LED led_237 (.in(panel_7_97c94c46_1__32_34));
  LED led_238 (.in(panel_7_97c94c46_1__33));
  LED led_239 (.in(panel_7_97c94c46_1__5));
  LED led_240 (.in(panel_7_97c94c46_1__10));
  LED led_241 (.in(panel_7_97c94c46_1__15));
  LED led_242 (.in(panel_7_97c94c46_1__20));
  LED led_243 (.in(panel_7_97c94c46_1__25));
  LED led_244 (.in(panel_7_97c94c46_1__30));
  LED led_245 (.in(panel_7_97c94c46_1__35));
  Panel_7_97c94c46 panel_7_97c94c46_1 (
    ._1_6(panel_7_97c94c46_1__1_6), ._2_4(panel_7_97c94c46_1__2_4), ._3(panel_7_97c94c46_1__3),
    ._5(panel_7_97c94c46_1__5), ._7(panel_7_97c94c46_1__7), ._8_28(panel_7_97c94c46_1__8_28),
    ._9_24(panel_7_97c94c46_1__9_24), ._10(panel_7_97c94c46_1__10), ._11(panel_7_97c94c46_1__11),
    ._13(panel_7_97c94c46_1__13), ._15(panel_7_97c94c46_1__15), ._16_21(panel_7_97c94c46_1__16_21),
    ._17(panel_7_97c94c46_1__17), ._18(panel_7_97c94c46_1__18), ._19(panel_7_97c94c46_1__19),
    ._20(panel_7_97c94c46_1__20), ._22(panel_7_97c94c46_1__22), ._23(panel_7_97c94c46_1__23),
    ._25(panel_7_97c94c46_1__25), ._26(panel_7_97c94c46_1__26), ._29(panel_7_97c94c46_1__29),
    ._30(panel_7_97c94c46_1__30), ._31(panel_7_97c94c46_1__31), ._32_34(panel_7_97c94c46_1__32_34),
    ._33(panel_7_97c94c46_1__33), ._35(panel_7_97c94c46_1__35));
endmodule
